// Logisim project camino_datos.circ as structural Verilog: 9 circuits, main circuit mux2_1_i1
module registro3 (
  input  [2:0] entrada,
  input  bit_en_desp,
  input  carga,
  input  desplaza,
  input  clk,
  input  reset,
  output [2:0] salida
);

  wire or_1_out;

  or or_1 (or_1_out, carga, desplaza);
  cdaff ff0 (
    .clk(clk), .carga(or_1_out), .inp_c(entrada[0]), .inp_d(salida[1]), .selc_d(carga), .reset(reset),
    .salida(salida[0]));
  cdaff ff1 (
    .clk(clk), .carga(or_1_out), .inp_c(entrada[1]), .inp_d(salida[2]), .selc_d(carga), .reset(reset),
    .salida(salida[1]));
  cdaff ff2 (
    .clk(clk), .carga(or_1_out), .inp_c(entrada[2]), .inp_d(bit_en_desp), .selc_d(carga), .reset(reset),
    .salida(salida[2]));
endmodule

// 1
module cdaff (
  input  clk,
  input  carga,
  input  reset,
  input  inp_c,
  input  inp_d,
  input  selc_d,
  output salida
);

  wire mux0_out;

  D_Flip_Flop ff0 (.clk(clk), .D(mux0_out), .Q(salida), .en(carga), .reset(reset));  // open: Qn, preset
  mux2_1_i1 mux0 (.s(selc_d), .a(inp_d), .b(inp_c), .out(mux0_out));
endmodule

module mux2_1_i1 (
  input  s,
  input  a,
  input  b,
  output out
);

  wire and1_out, and2_out, not_1_out;

  not not_1 (not_1_out, s);
  and and1 (and1_out, not_1_out, a);
  and and2 (and2_out, s, b);
  or or1 (out, and1_out, and2_out);
endmodule

module registro4 (
  input  [3:0] entrada,
  input  bit_en_desp,
  input  carga,
  input  desplaza,
  input  clk,
  input  reset,
  output [3:0] salida
);

  wire or_1_out;

  or or_1 (or_1_out, carga, desplaza);
  cdaff ff0 (
    .clk(clk), .carga(or_1_out), .inp_c(entrada[0]), .inp_d(salida[1]), .selc_d(carga), .reset(reset),
    .salida(salida[0]));
  cdaff ff1 (
    .clk(clk), .carga(or_1_out), .inp_c(entrada[1]), .inp_d(salida[2]), .selc_d(carga), .reset(reset),
    .salida(salida[1]));
  cdaff ff2 (
    .clk(clk), .carga(or_1_out), .inp_c(entrada[2]), .inp_d(salida[3]), .selc_d(carga), .reset(reset),
    .salida(salida[2]));
  cdaff ff3 (
    .clk(clk), .carga(or_1_out), .inp_c(entrada[3]), .inp_d(bit_en_desp), .selc_d(carga), .reset(reset),
    .salida(salida[3]));
endmodule

module cd (
  input  M2,
  input  M1,
  input  M0,
  input  carga_A,
  input  carga_Q,
  input  carga_M,
  input  clk,
  input  reset_A,
  input  reset,
  input  desplaza_A,
  input  m2_2,
  input  m1_2,
  input  m0_2,
  input  desplaza_M,
  input  desplaza_Q,
  input  suma_resta,
  output [2:0] salida_Q,
  output q_1,
  output [3:0] salida_A,
  output [3:0] mi_resul,
  output [3:0] salida_M,
  output [3:0] salida_suma_resta
);

  wire or_1_out;

  registro4 A (
    .entrada(salida_suma_resta), .bit_en_desp(salida_A[3]), .carga(carga_A), .desplaza(desplaza_A),
    .clk(clk), .reset(reset_A), .salida({salida_A[3:1], mi_resul[3]}));
  registro4 M (
    .entrada({{2{m2_2}}, m1_2, m0_2}), .bit_en_desp(1'b0), .carga(carga_M), .desplaza(desplaza_M), .clk(clk),
    .reset(reset), .salida(salida_M));
  suma_resta4 suma_resta4_1 (
    .A({salida_A[3:1], mi_resul[3]}), .B(salida_M), .salida(salida_suma_resta), .suma_resta(suma_resta));
  registro3 Q (
    .entrada({M2, M1, M0}), .bit_en_desp(mi_resul[3]), .carga(carga_Q), .desplaza(desplaza_Q), .clk(clk),
    .reset(reset), .salida(mi_resul[2:0]));
  or or_1 (or_1_out, carga_Q, desplaza_Q);
  D_Flip_Flop u_Q_1 (.clk(clk), .D(mi_resul[0]), .Q(q_1), .en(or_1_out), .reset(reset));  // open: Qn, preset

  assign salida_A[0] = mi_resul[3];
  assign salida_Q = mi_resul[2:0];
endmodule

module suma_resta4 (
  input  [3:0] A,
  input  [3:0] B,
  input  suma_resta,
  output [3:0] salida
);

  wire [3:0] multiplexer_1_out, negator_1_out;

  Negator #(.width(4)) negator_1 (.in(B), .out(negator_1_out));
  Multiplexer #(.width(4)) multiplexer_1 (
    .in0(B), .in1(negator_1_out), .out(multiplexer_1_out), .sel(suma_resta), .en(1'b1));
  Adder #(.width(4)) adder_1 (.a(A), .b(multiplexer_1_out), .out(salida));  // open: cin, cout
endmodule

// counter_states
module states (
  input  clk,
  input  reset,
  output _0,
  output _1,
  output _2
);

  wire not_1_out, not_2_out;

  not not_1 (not_1_out, _0);
  J_K_Flip_Flop j_k_ff_1 (.J(1'b1), .clk(clk), .K(1'b1), .Q(_0), .reset(reset));  // open: Qn, preset, en
  J_K_Flip_Flop j_k_ff_2 (.J(1'b1), .clk(not_1_out), .K(1'b1), .Q(_1), .reset(reset));  // open: Qn, preset, en
  not not_2 (not_2_out, _1);
  J_K_Flip_Flop j_k_ff_3 (.J(1'b1), .clk(not_2_out), .K(1'b1), .Q(_2), .reset(reset));  // open: Qn, preset, en
endmodule

module uc (
  input  reset,
  input  clk,
  input  q_1,
  input  q_0,
  output fin,
  output carga_M,
  output reset_A,
  output desplaza,
  output carga_Q,
  output suma,
  output carga_A
);

  wire and_1_out, not_1_out, not_2_out, not_3_out, not_4_out, not_5_out, not_6_out, not_7_out, not_8_out,
       not_9_out, not_10_out, not_11_out, not_12_out, not_13_out, not_14_out, not_15_out, not_16_out,
       or_1_out, or_2_out, resta_out, s1_out, s2_out, s3_out, s4_out, s5_out, s6_out, states_1__0,
       states_1__1, states_1__2, suma_out;

  not not_1 (not_1_out, q_1);
  not not_2 (not_2_out, q_0);
  states states_1 (.clk(and_1_out), .reset(reset), ._0(states_1__0), ._1(states_1__1), ._2(states_1__2));
  and and_1 (and_1_out, clk, not_3_out);
  not not_3 (not_3_out, fin);
  and u_suma (suma_out, q_1, not_2_out);
  and resta (resta_out, not_1_out, q_0);
  and s7 (fin, states_1__0, states_1__1, states_1__2);
  not not_4 (not_4_out, states_1__0);
  or or_1 (or_1_out, s1_out, s3_out, s5_out);
  or or_2 (or_2_out, suma_out, resta_out);
  not not_5 (not_5_out, suma_out);
  and s6 (s6_out, not_4_out, states_1__1, states_1__2);
  and and_2 (carga_A, or_1_out, or_2_out);
  or or_3 (suma, not_5_out, resta_out);
  not not_6 (not_6_out, states_1__1);
  and s5 (s5_out, states_1__0, not_6_out, states_1__2);
  not not_7 (not_7_out, states_1__1);
  not not_8 (not_8_out, states_1__0);
  and s4 (s4_out, not_8_out, states_1__2);
  or or_4 (desplaza, s6_out, s4_out, s2_out);
  not not_9 (not_9_out, states_1__2);
  and s3 (s3_out, states_1__0, states_1__1, not_9_out);
  not not_10 (not_10_out, states_1__0);
  not not_11 (not_11_out, states_1__2);
  and s2 (s2_out, not_10_out, states_1__1, not_11_out);
  not not_12 (not_12_out, states_1__2);
  not not_13 (not_13_out, states_1__1);
  and s1 (s1_out, states_1__0, not_13_out, not_12_out);
  not not_14 (not_14_out, states_1__0);
  not not_15 (not_15_out, states_1__1);
  not not_16 (not_16_out, states_1__2);
  and s0 (carga_M, not_14_out, not_15_out, not_16_out);

  assign carga_Q = carga_M;
  assign reset_A = carga_M;
endmodule

module multiplicador (
  input  M2,
  input  M1,
  input  M0,
  input  clk,
  input  reset,
  input  m2_2,
  input  m1_2,
  input  m0_2,
  output fin,
  output [3:0] out_10,
  output [3:0] contenido_A,
  output [2:0] contenido_Q,
  output q_1
);

  wire uc_1_carga_a, uc_1_carga_m, uc_1_carga_q, uc_1_desplaza, uc_1_reset_a, uc_1_suma;

  cd cd_1 (
    .q_1(q_1), .mi_resul(out_10), .clk(clk), .reset_A(uc_1_reset_a), .reset(reset),
    .desplaza_A(uc_1_carga_a), .desplaza_Q(uc_1_carga_a), .carga_A(uc_1_desplaza), .carga_Q(uc_1_carga_q),
    .carga_M(uc_1_carga_m), .m2_2(m2_2), .m1_2(m1_2), .m0_2(m0_2), .M2(M2), .M1(M1), .M0(M0),
    .salida_Q(contenido_Q), .salida_A(contenido_A), .suma_resta(uc_1_suma));  // open: desplaza_M, salida_M, salida_suma_resta
  uc uc_1 (
    .reset(reset), .clk(clk), .q_1(q_1), .q_0(contenido_Q[0]), .fin(fin), .suma(uc_1_suma),
    .desplaza(uc_1_desplaza), .carga_A(uc_1_carga_a), .carga_M(uc_1_carga_m), .carga_Q(uc_1_carga_q),
    .reset_A(uc_1_reset_a));
endmodule
